# Fritzing sketch Clockduino (saved by Fritzing 0.7.12b)
breadboards: 1

parts:
  LCD1 = Adafruit Negative RGB 2x16 LCD
  Red_Brightness_Knob = Breadboard Trimpot
  Green_Brightness_Knob = Breadboard Trimpot
  Blue_Brightness_Knob = Breadboard Trimpot
  Total_Brightness_Knob = Breadboard Trimpot
  Temperature_Sensor = DS18B20 1-Wire Temperature Sensor [part_number=DS18B20]
  Contrast_Adjustment_Knob = Breadboard Trimpot
  I2C_IO_Expander_for_LCD = Microchip MCP23008 8-bit I/O expander [part_number=MCP23008 package="DIP (Dual Inline) [THT]"]
  Arduino1 = Arduino
  Data_Logging_Sheild = DS1307 RTC Breakout
  R1 = Resistor [tolerance=±5% resistance=4.7k package=THT]
  R2 = Resistor [tolerance=±5% resistance=10k package=THT]
  Simple_RF_M4_Receiver_315Mhz = mystery part, 7 pins [chip_label=R02A]

nets:
  GND: LCD1.no_name_yet#0, LCD1.no_name_yet#4, Red_Brightness_Knob.PIN3, Green_Brightness_Knob.PIN3, Blue_Brightness_Knob.PIN3, Total_Brightness_Knob.PIN3, Temperature_Sensor.GND, Contrast_Adjustment_Knob.PIN3, I2C_IO_Expander_for_LCD.A2, I2C_IO_Expander_for_LCD.A1, I2C_IO_Expander_for_LCD.A0, I2C_IO_Expander_for_LCD.VSS, Arduino1.GND, Data_Logging_Sheild.GND, Simple_RF_M4_Receiver_315Mhz.pin1
  5V: LCD1.no_name_yet#1, LCD1.no_name_yet#14, Red_Brightness_Knob.PIN1, Green_Brightness_Knob.PIN1, Blue_Brightness_Knob.PIN1, Total_Brightness_Knob.PIN1, Temperature_Sensor.VDD, Contrast_Adjustment_Knob.PIN1, I2C_IO_Expander_for_LCD.VDD, Arduino1.+5V, Data_Logging_Sheild.5V, R1.Pin_0, R2.Pin_0, Simple_RF_M4_Receiver_315Mhz.pin2
  N1: LCD1.no_name_yet#2, Contrast_Adjustment_Knob.PIN2
  N2: LCD1.no_name_yet#3, I2C_IO_Expander_for_LCD.GP1
  N3: LCD1.no_name_yet#5, I2C_IO_Expander_for_LCD.GP2
  LCD DB4: LCD1.no_name_yet#10, I2C_IO_Expander_for_LCD.GP3
  LCD DB5: LCD1.no_name_yet#11, I2C_IO_Expander_for_LCD.GP4
  LCD DB6: LCD1.no_name_yet#12, I2C_IO_Expander_for_LCD.GP5
  LCD DB7: LCD1.no_name_yet#13, I2C_IO_Expander_for_LCD.GP6
  Red PWM: LCD1.no_name_yet#15, Arduino1.D3
  Green PWM: LCD1.no_name_yet#16, Arduino1.D9
  Blue PWM: LCD1.no_name_yet#17, Arduino1.D11
  N4: Red_Brightness_Knob.PIN2, Arduino1.A0
  N5: Green_Brightness_Knob.PIN2, Arduino1.A1
  N6: Blue_Brightness_Knob.PIN2, Arduino1.A2
  N7: Total_Brightness_Knob.PIN2, Arduino1.A3
  OneWire: Temperature_Sensor.DQ, Arduino1.D5, R1.Pin_1
  SCL: I2C_IO_Expander_for_LCD.SCL, Arduino1.SCL, Data_Logging_Sheild.SCL
  SDA: I2C_IO_Expander_for_LCD.SDA, Arduino1.SDA, Data_Logging_Sheild.SDA
  N8: I2C_IO_Expander_for_LCD.Reset, R2.Pin_1
  N9: Arduino1.D2, Simple_RF_M4_Receiver_315Mhz.pin6

notes:
  The DS1307 Breakout is substitued for the Adafruit Data Logging Shield - SD Card currently not used.
  Bus Wiring Key
  Red: +5 Volts
  Black: Ground
  Yellow: 5 Volt Logic Bus
  Purple: I2C Data Bus
  Brown: I2C Clock Bus
  White: One Wire Bus
  Grey: Analog Bus
  Mystery Part R02A:
  Simple RF M4 Receiver
  Momentary Type
  315Mhz
  PWM Output Wires
  Red -> Red
  Green -> Green
  Blue -> Blue
  Other -> No PWM

custom parts:
  Adafruit Negative RGB 2x16 LCD: Adafruit Negative 2x16 LCD Display with RGB Backlight
  Microchip MCP23008 8-bit I/O expander: Provides 8-bit, general purpose, parallel I/O expansion for I2C bus. Datasheet: http://ww1.microchip.com/downloads/en/devicedoc/21919e.pdf
  DS1307 RTC Breakout: DS1307 Real-time Clock Breakout Board with Battery
